// Logisim project 7400_Series.circ as structural Verilog: 10 circuits, main circuit SN74HC138
module SN74HC138 (
  input  A2,
  input  A1,
  input  A0,
  input  E1,
  input  E2,
  input  E3,
  output Y7,
  output Y6,
  output Y5,
  output Y4,
  output Y3,
  output Y2,
  output Y1,
  output Y0
);

  wire and_1_out, and_2_out, and_3_out, and_4_out, and_5_out, and_6_out, and_7_out, and_8_out, and_9_out,
       not_1_out, not_2_out, not_3_out, not_4_out, not_5_out, not_6_out, not_7_out, not_8_out;

  not not_1 (not_1_out, A2);
  not not_2 (not_2_out, A1);
  not not_3 (not_3_out, A0);
  not not_4 (not_4_out, E1);
  not not_5 (not_5_out, E2);
  and and_1 (and_1_out, not_4_out, not_5_out, E3);
  not not_6 (not_6_out, not_1_out);
  not not_7 (not_7_out, not_2_out);
  not not_8 (not_8_out, not_3_out);
  and and_2 (and_2_out, not_8_out, not_7_out, not_6_out, and_1_out);
  and and_3 (and_3_out, not_3_out, not_6_out, not_7_out, and_1_out);
  and and_4 (and_4_out, not_8_out, not_6_out, not_2_out, and_1_out);
  and and_5 (and_5_out, not_6_out, not_2_out, not_3_out, and_1_out);
  and and_6 (and_6_out, not_7_out, not_8_out, not_1_out, and_1_out);
  and and_7 (and_7_out, not_7_out, not_3_out, not_1_out, and_1_out);
  and and_8 (and_8_out, not_8_out, not_2_out, not_1_out, and_1_out);
  and and_9 (and_9_out, and_1_out, not_1_out, not_2_out, not_3_out);
  not not_9 (Y7, and_2_out);
  not not_10 (Y6, and_3_out);
  not not_11 (Y5, and_4_out);
  not not_12 (Y4, and_5_out);
  not not_13 (Y3, and_6_out);
  not not_14 (Y2, and_7_out);
  not not_15 (Y1, and_8_out);
  not not_16 (Y0, and_9_out);
endmodule

module SN74HC244 (
  input  A1,
  input  A2,
  input  A3,
  input  A4,
  input  ENA,
  input  B1,
  input  B2,
  input  B3,
  input  B6,
  input  ENB,
  output YA1,
  output YA2,
  output YA3,
  output YA4,
  output YB1,
  output YB2,
  output YB3,
  output YB4
);

  wire not_1_out, not_2_out;

  not not_1 (not_1_out, ENA);
  not not_2 (not_2_out, ENB);
  assign YA1 = not_1_out ? A1 : 1'bz;  // Controlled_Buffer controlled_buffer_1
  assign YA2 = not_1_out ? A2 : 1'bz;  // Controlled_Buffer controlled_buffer_2
  assign YA3 = not_1_out ? A3 : 1'bz;  // Controlled_Buffer controlled_buffer_3
  assign YA4 = not_1_out ? A4 : 1'bz;  // Controlled_Buffer controlled_buffer_4
  assign YB1 = not_2_out ? B1 : 1'bz;  // Controlled_Buffer controlled_buffer_5
  assign YB2 = not_2_out ? B2 : 1'bz;  // Controlled_Buffer controlled_buffer_6
  assign YB3 = not_2_out ? B3 : 1'bz;  // Controlled_Buffer controlled_buffer_7
  assign YB4 = not_2_out ? B6 : 1'bz;  // Controlled_Buffer controlled_buffer_8
endmodule

module SN74HC273 (
  input  CLK,
  input  D1,
  input  D2,
  input  D3,
  input  D4,
  input  D5,
  input  D6,
  input  D7,
  input  D8,
  input  CLRn,
  output Q1,
  output Q2,
  output Q3,
  output Q4,
  output Q5,
  output Q6,
  output Q7,
  output Q8
);

  xxD_FF_PC xxd_ff_pc_1 (.PRE(1'b1), .D(D1), .C(CLK), .CLR(CLRn), .Q(Q1));  // open: Qn
  xxD_FF_PC xxd_ff_pc_2 (.PRE(1'b1), .D(D2), .C(CLK), .CLR(CLRn), .Q(Q2));  // open: Qn
  xxD_FF_PC xxd_ff_pc_3 (.PRE(1'b1), .D(D3), .C(CLK), .CLR(CLRn), .Q(Q3));  // open: Qn
  xxD_FF_PC xxd_ff_pc_4 (.PRE(1'b1), .D(D4), .C(CLK), .CLR(CLRn), .Q(Q4));  // open: Qn
  xxD_FF_PC xxd_ff_pc_5 (.PRE(1'b1), .D(D5), .C(CLK), .CLR(CLRn), .Q(Q5));  // open: Qn
  xxD_FF_PC xxd_ff_pc_6 (.PRE(1'b1), .D(D6), .C(CLK), .CLR(CLRn), .Q(Q6));  // open: Qn
  xxD_FF_PC xxd_ff_pc_7 (.PRE(1'b1), .D(D7), .C(CLK), .CLR(CLRn), .Q(Q7));  // open: Qn
  xxD_FF_PC xxd_ff_pc_8 (.PRE(1'b1), .D(D8), .C(CLK), .CLR(CLRn), .Q(Q8));  // open: Qn
endmodule

module xxD_FF_PC (
  input  PRE,
  input  D,
  input  C,
  input  CLR,
  output Q,
  output Qn
);

  wire nand_1_out, nand_2_out, not_1_out;

  not not_1 (not_1_out, D);
  nand nand_1 (nand_1_out, D, C);
  nand nand_2 (nand_2_out, C, not_1_out);
  nand nand_3 (Q, PRE, nand_1_out, Qn);
  nand nand_4 (Qn, Q, nand_2_out, CLR);
endmodule

module SN74HC373 (
  input  OE,
  input  LE,
  input  D1,
  input  D2,
  input  D3,
  input  D4,
  input  D5,
  input  D6,
  input  D7,
  input  D8,
  output Y1,
  output Y2,
  output Y3,
  output Y4,
  output Y5,
  output Y6,
  output Y7,
  output Y8
);

  wire sn74hc273_1_q1, sn74hc273_1_q2, sn74hc273_1_q3, sn74hc273_1_q4, sn74hc273_1_q5, sn74hc273_1_q6,
       sn74hc273_1_q7, sn74hc273_1_q8;

  SN74HC273 sn74hc273_1 (
    .CLK(LE), .D1(D1), .D2(D2), .D3(D3), .D4(D4), .D5(D5), .D6(D6), .D7(D7), .D8(D8), .CLRn(1'b1),
    .Q1(sn74hc273_1_q1), .Q2(sn74hc273_1_q2), .Q3(sn74hc273_1_q3), .Q4(sn74hc273_1_q4), .Q5(sn74hc273_1_q5),
    .Q6(sn74hc273_1_q6), .Q7(sn74hc273_1_q7), .Q8(sn74hc273_1_q8));
  SN74HC244 sn74hc244_1 (
    .A1(sn74hc273_1_q1), .A2(sn74hc273_1_q2), .A3(sn74hc273_1_q3), .A4(sn74hc273_1_q4), .ENA(OE),
    .B1(sn74hc273_1_q5), .B2(sn74hc273_1_q6), .B3(sn74hc273_1_q7), .B6(sn74hc273_1_q8), .ENB(OE), .YA1(Y1),
    .YA2(Y2), .YA3(Y3), .YA4(Y4), .YB1(Y5), .YB2(Y6), .YB3(Y7), .YB4(Y8));
endmodule

module SN74HC139 (
  input  A0,
  input  A2,
  input  EA,
  input  B0,
  input  B1,
  input  EB,
  output YA0,
  output YA1,
  output YA2,
  output YA3,
  output YB0,
  output YB1,
  output YB2,
  output YB3
);

  wire nand_1_out, nand_2_out, nand_3_out, nand_4_out, nand_5_out, nand_6_out, nand_7_out, nand_8_out,
       not_1_out, not_2_out, not_3_out, not_4_out, not_5_out, not_6_out, not_7_out, not_8_out, not_9_out,
       not_10_out, not_11_out, not_12_out, not_13_out, not_14_out, not_15_out, not_16_out, not_17_out,
       not_18_out;

  not not_1 (not_1_out, A0);
  not not_2 (not_2_out, A2);
  not not_3 (not_3_out, EA);
  not not_4 (not_4_out, B0);
  not not_5 (not_5_out, B1);
  not not_6 (not_6_out, EB);
  not not_7 (not_7_out, not_1_out);
  not not_8 (not_8_out, not_2_out);
  not not_9 (not_9_out, not_4_out);
  not not_10 (not_10_out, not_5_out);
  nand nand_1 (nand_1_out, not_1_out, not_2_out, not_3_out);
  nand nand_2 (nand_2_out, not_7_out, not_2_out, not_3_out);
  nand nand_3 (nand_3_out, not_1_out, not_8_out, not_3_out);
  nand nand_4 (nand_4_out, not_7_out, not_8_out, not_3_out);
  nand nand_5 (nand_5_out, not_4_out, not_5_out, not_6_out);
  nand nand_6 (nand_6_out, not_9_out, not_5_out, not_6_out);
  nand nand_7 (nand_7_out, not_4_out, not_10_out, not_6_out);
  nand nand_8 (nand_8_out, not_9_out, not_10_out, not_6_out);
  not not_11 (not_11_out, nand_1_out);
  not not_12 (not_12_out, nand_2_out);
  not not_13 (not_13_out, nand_3_out);
  not not_14 (not_14_out, nand_4_out);
  not not_15 (not_15_out, nand_5_out);
  not not_16 (not_16_out, nand_6_out);
  not not_17 (not_17_out, nand_7_out);
  not not_18 (not_18_out, nand_8_out);
  not not_19 (YA0, not_11_out);
  not not_20 (YA1, not_12_out);
  not not_21 (YA2, not_13_out);
  not not_22 (YA3, not_14_out);
  not not_23 (YB0, not_15_out);
  not not_24 (YB1, not_16_out);
  not not_25 (YB2, not_17_out);
  not not_26 (YB3, not_18_out);
endmodule

module SN74HC148 (
  input  in_1,
  input  in_2,
  input  in_3,
  input  in_4,
  input  in_5,
  input  in_6,
  input  in_7,
  input  in_8,
  input  in_9,
  output EO,
  output GS,
  output A0,
  output A1,
  output A2
);

  wire and_1_out, and_2_out, and_3_out, and_4_out, and_5_out, and_6_out, and_7_out, and_8_out, and_9_out,
       and_10_out, and_11_out, and_12_out, not_1_out, not_2_out, not_3_out, not_4_out, not_5_out, not_6_out,
       not_7_out, not_8_out, not_9_out, not_10_out, not_11_out, not_12_out, not_13_out, not_14_out;

  not not_1 (not_1_out, in_2);
  not not_2 (not_2_out, in_3);
  not not_3 (not_3_out, in_4);
  not not_4 (not_4_out, in_5);
  not not_5 (not_5_out, in_6);
  not not_6 (not_6_out, in_7);
  not not_7 (not_7_out, in_8);
  not not_8 (not_8_out, in_9);
  not not_9 (not_9_out, not_2_out);
  not not_10 (not_10_out, not_4_out);
  not not_11 (not_11_out, not_5_out);
  not not_12 (not_12_out, not_6_out);
  nand nand_1 (EO, in_1, in_2, in_3, in_4, in_5, in_6, in_7, in_8, not_8_out);
  and and_1 (and_1_out, not_1_out, not_9_out, not_10_out, not_12_out, not_8_out);
  and and_2 (and_2_out, not_3_out, not_10_out, not_12_out, not_8_out);
  and and_3 (and_3_out, not_5_out, not_12_out, not_8_out);
  and and_4 (and_4_out, not_7_out, not_8_out);
  and and_5 (and_5_out, not_2_out, not_10_out, not_11_out, not_8_out);
  and and_6 (and_6_out, not_3_out, not_10_out, not_11_out, not_8_out);
  and and_7 (and_7_out, not_6_out, not_8_out);
  and and_8 (and_8_out, not_7_out, not_8_out);
  and and_9 (and_9_out, not_4_out, not_8_out);
  and and_10 (and_10_out, not_5_out, not_8_out);
  and and_11 (and_11_out, not_6_out, not_8_out);
  and and_12 (and_12_out, not_7_out, not_8_out);
  not not_13 (not_13_out, EO);
  not not_14 (not_14_out, not_8_out);
  or or_1 (GS, not_13_out, not_14_out);
  nor nor_1 (A0, and_1_out, and_2_out, and_3_out, and_4_out);
  nor nor_2 (A1, and_5_out, and_6_out, and_7_out, and_8_out);
  nor nor_3 (A2, and_9_out, and_10_out, and_11_out, and_12_out);
endmodule

module SN74HC147 (
  input  I1,
  input  I2,
  input  I3,
  input  I4,
  input  I5,
  input  I6,
  input  I7,
  input  I8,
  input  I9,
  output Y3,
  output Y2,
  output Y1,
  output Y0
);

  wire and_2_out, and_3_out, and_4_out, and_5_out, and_6_out, and_7_out, and_8_out, and_9_out, and_10_out,
       not_1_out, not_2_out, not_3_out, not_4_out, not_5_out, not_6_out;

  not not_1 (not_1_out, I2);
  not not_2 (not_2_out, I4);
  not not_3 (not_3_out, I5);
  not not_4 (not_4_out, I6);
  not not_5 (not_5_out, I8);
  not not_6 (not_6_out, I9);
  and and_1 (Y3, I8, I9);
  and and_2 (and_2_out, I4, I5, I6, I7);
  and and_3 (and_3_out, not_2_out, I6, I7);
  and and_4 (and_4_out, not_3_out, I6, I7);
  and and_5 (and_5_out, I2, I3, I6, I7);
  and and_6 (and_6_out, not_5_out, I9);
  and and_7 (and_7_out, not_4_out, I7, I9);
  and and_8 (and_8_out, not_2_out, I5, I7, I9);
  and and_9 (and_9_out, not_1_out, I3, I5, I7, I9);
  and and_10 (and_10_out, I1, I3, I5, I7, I9);
  or or_1 (Y2, not_5_out, not_6_out, and_2_out);
  or or_2 (Y1, not_5_out, not_6_out, and_3_out, and_4_out, and_5_out);
  or or_3 (Y0, and_6_out, and_7_out, and_8_out, and_9_out, and_10_out);
endmodule

module SN74HC299 (
  input  S0,
  input  S1,
  input  SLIN,
  input  SRIN,
  input  CLK,
  input  xQA,
  input  xOH,
  input  CLR,
  input  G1,
  input  G2,
  output QA,
  output QB,
  output QC,
  output QD,
  output QE,
  output QF,
  output QG,
  output QH
);

  wire and_1_out, and_2_out, and_3_out, and_4_out, and_5_out, and_6_out, and_7_out, and_8_out, and_9_out,
       and_10_out, and_11_out, and_12_out, and_13_out, and_14_out, and_15_out, and_16_out, and_17_out,
       and_18_out, and_19_out, and_20_out, and_21_out, and_22_out, and_23_out, and_24_out, and_25_out,
       and_26_out, and_27_out, and_28_out, and_29_out, and_30_out, and_31_out, and_32_out, and_33_out,
       nor_1_out, not_1_out, not_2_out, not_3_out, not_4_out, not_5_out, not_6_out, not_7_out, not_8_out,
       not_9_out, not_10_out, or_1_out, or_2_out, or_3_out, or_4_out, or_5_out, or_6_out, or_7_out, or_8_out,
       undriven, undriven_2, xxd_ff_pc_2_q, xxd_ff_pc_3_q, xxd_ff_pc_4_q, xxd_ff_pc_5_q, xxd_ff_pc_6_q,
       xxd_ff_pc_7_q;

  not not_1 (not_1_out, CLK);
  not not_2 (not_2_out, S0);
  not not_3 (not_3_out, S1);
  not not_4 (not_4_out, S1);
  not not_5 (not_5_out, S0);
  not not_6 (not_6_out, not_2_out);
  not not_7 (not_7_out, not_3_out);
  nor nor_1 (nor_1_out, not_4_out, not_5_out);
  not not_8 (not_8_out, nor_1_out);
  not not_9 (not_9_out, G1);
  not not_10 (not_10_out, G2);
  and and_1 (and_1_out, SRIN, not_6_out, not_3_out);
  and and_2 (and_2_out, not_8_out, not_9_out, not_10_out);
  and and_3 (and_3_out, not_7_out, not_2_out, xxd_ff_pc_2_q);
  or or_1 (or_1_out, and_1_out, and_3_out, and_4_out, and_5_out);
  and and_4 (and_4_out, not_7_out, not_6_out, QA);
  and and_5 (and_5_out, not_3_out, not_2_out, xQA);
  xxD_FF_PC xxd_ff_pc_1 (.PRE(1'b1), .D(or_1_out), .C(not_1_out), .CLR(CLR), .Q(xQA));  // open: Qn
  assign QA = and_2_out ? xQA : 1'bz;  // Controlled_Buffer controlled_buffer_1
  and and_6 (and_6_out, xQA, not_6_out, not_3_out);
  and and_7 (and_7_out, not_7_out, not_2_out, xxd_ff_pc_3_q);
  or or_2 (or_2_out, and_6_out, and_7_out, and_8_out, and_9_out);
  and and_8 (and_8_out, not_7_out, not_6_out, QB);
  and and_9 (and_9_out, not_3_out, not_2_out, xxd_ff_pc_2_q);
  xxD_FF_PC xxd_ff_pc_2 (.PRE(1'b1), .D(or_2_out), .C(not_1_out), .CLR(CLR), .Q(xxd_ff_pc_2_q));  // open: Qn
  assign QB = and_2_out ? xxd_ff_pc_2_q : 1'bz;  // Controlled_Buffer controlled_buffer_2
  and and_10 (and_10_out, xxd_ff_pc_2_q, not_6_out, not_3_out);
  and and_11 (and_11_out, not_7_out, not_2_out, xxd_ff_pc_4_q);
  and and_12 (and_12_out, not_7_out, not_6_out, QC);
  or or_3 (or_3_out, and_10_out, and_11_out, and_12_out, and_13_out);
  and and_13 (and_13_out, not_3_out, not_2_out, xxd_ff_pc_3_q);
  xxD_FF_PC xxd_ff_pc_3 (.PRE(1'b1), .D(or_3_out), .C(not_1_out), .CLR(CLR), .Q(xxd_ff_pc_3_q));  // open: Qn
  assign QC = and_2_out ? xxd_ff_pc_3_q : 1'bz;  // Controlled_Buffer controlled_buffer_3
  and and_14 (and_14_out, xxd_ff_pc_3_q, not_6_out, not_3_out);
  and and_15 (and_15_out, not_7_out, not_2_out, xxd_ff_pc_5_q);
  and and_16 (and_16_out, not_7_out, not_6_out, QD);
  or or_4 (or_4_out, and_14_out, and_15_out, and_16_out, and_17_out);
  and and_17 (and_17_out, not_3_out, not_2_out, xxd_ff_pc_4_q);
  xxD_FF_PC xxd_ff_pc_4 (.PRE(1'b1), .D(or_4_out), .C(not_1_out), .CLR(CLR), .Q(xxd_ff_pc_4_q));  // open: Qn
  assign QD = and_2_out ? xxd_ff_pc_4_q : 1'bz;  // Controlled_Buffer controlled_buffer_4
  and and_18 (and_18_out, xxd_ff_pc_4_q, not_6_out, not_3_out);
  and and_19 (and_19_out, not_7_out, not_2_out, undriven);
  and and_20 (and_20_out, not_7_out, not_6_out, QE);
  or or_5 (or_5_out, and_18_out, and_19_out, and_20_out, and_21_out);
  and and_21 (and_21_out, not_3_out, not_2_out, xxd_ff_pc_5_q);
  xxD_FF_PC xxd_ff_pc_5 (.PRE(1'b1), .D(or_5_out), .C(not_1_out), .CLR(CLR), .Q(xxd_ff_pc_5_q));  // open: Qn
  assign QE = and_2_out ? xxd_ff_pc_5_q : 1'bz;  // Controlled_Buffer controlled_buffer_5
  and and_22 (and_22_out, xxd_ff_pc_5_q, not_6_out, not_3_out);
  and and_23 (and_23_out, not_7_out, not_2_out, xxd_ff_pc_7_q);
  and and_24 (and_24_out, not_7_out, not_6_out, QF);
  or or_6 (or_6_out, and_22_out, and_23_out, and_24_out, and_25_out);
  and and_25 (and_25_out, not_3_out, not_2_out, xxd_ff_pc_6_q);
  xxD_FF_PC xxd_ff_pc_6 (.PRE(1'b1), .D(or_6_out), .C(undriven_2), .CLR(CLR), .Q(xxd_ff_pc_6_q));  // open: Qn
  assign QF = and_2_out ? xxd_ff_pc_6_q : 1'bz;  // Controlled_Buffer controlled_buffer_6
  and and_26 (and_26_out, xxd_ff_pc_6_q, not_6_out, not_3_out);
  and and_27 (and_27_out, not_7_out, not_2_out, xOH);
  and and_28 (and_28_out, not_7_out, not_6_out, QG);
  or or_7 (or_7_out, and_26_out, and_27_out, and_28_out, and_29_out);
  and and_29 (and_29_out, not_3_out, not_2_out, xxd_ff_pc_7_q);
  xxD_FF_PC xxd_ff_pc_7 (.PRE(1'b1), .D(or_7_out), .C(undriven_2), .CLR(CLR), .Q(xxd_ff_pc_7_q));  // open: Qn
  assign QG = and_2_out ? xxd_ff_pc_7_q : 1'bz;  // Controlled_Buffer controlled_buffer_7
  and and_30 (and_30_out, xxd_ff_pc_7_q, not_6_out, not_3_out);
  and and_31 (and_31_out, not_7_out, not_2_out, SLIN);
  and and_32 (and_32_out, not_7_out, not_6_out, QH);
  and and_33 (and_33_out, not_3_out, not_2_out, xOH);
  or or_8 (or_8_out, and_30_out, and_31_out, and_32_out, and_33_out);
  xxD_FF_PC xxd_ff_pc_8 (.PRE(1'b1), .D(or_8_out), .C(undriven_2), .CLR(CLR), .Q(xOH));  // open: Qn
  assign QH = and_2_out ? xOH : 1'bz;  // Controlled_Buffer controlled_buffer_8
endmodule

module SN74HC245 (
  input  DIR,
  input  OEn,
  input  A0i,
  input  B0i,
  input  A1i,
  input  B1i,
  input  A2i,
  input  B2i,
  input  A3i,
  input  B3i,
  input  A4i,
  input  B4i,
  input  A5i,
  input  B5i,
  input  A6i,
  input  B6i,
  input  A7i,
  input  B7i,
  output B0o,
  output A0o,
  output B1o,
  output A1o,
  output B2o,
  output A2o,
  output B3o,
  output A3o,
  output B4o,
  output A4o,
  output B5o,
  output A5o,
  output B6o,
  output A6o,
  output B7o,
  output A7o
);

  wire and_1_out, and_2_out, not_1_out, not_2_out, not_3_out;

  not not_1 (not_1_out, OEn);
  and and_1 (and_1_out, DIR, not_1_out);
  assign B0o = and_1_out ? A0i : 1'bz;  // Controlled_Buffer controlled_buffer_1
  assign B1o = and_1_out ? A1i : 1'bz;  // Controlled_Buffer controlled_buffer_2
  assign B2o = and_1_out ? A2i : 1'bz;  // Controlled_Buffer controlled_buffer_3
  assign B3o = and_1_out ? A3i : 1'bz;  // Controlled_Buffer controlled_buffer_4
  assign B4o = and_1_out ? A4i : 1'bz;  // Controlled_Buffer controlled_buffer_5
  assign B5o = and_1_out ? A5i : 1'bz;  // Controlled_Buffer controlled_buffer_6
  assign B6o = and_1_out ? A6i : 1'bz;  // Controlled_Buffer controlled_buffer_7
  assign B7o = and_1_out ? A7i : 1'bz;  // Controlled_Buffer controlled_buffer_8
  and and_2 (and_2_out, not_2_out, not_3_out);
  assign A0o = and_2_out ? B0i : 1'bz;  // Controlled_Buffer controlled_buffer_9
  assign A1o = and_2_out ? B1i : 1'bz;  // Controlled_Buffer controlled_buffer_10
  assign A2o = and_2_out ? B2i : 1'bz;  // Controlled_Buffer controlled_buffer_11
  assign A3o = and_2_out ? B3i : 1'bz;  // Controlled_Buffer controlled_buffer_12
  assign A4o = and_2_out ? B4i : 1'bz;  // Controlled_Buffer controlled_buffer_13
  assign A5o = and_2_out ? B5i : 1'bz;  // Controlled_Buffer controlled_buffer_14
  assign A6o = and_2_out ? B6i : 1'bz;  // Controlled_Buffer controlled_buffer_15
  assign A7o = and_2_out ? B7i : 1'bz;  // Controlled_Buffer controlled_buffer_16
  not not_2 (not_2_out, DIR);
  not not_3 (not_3_out, OEn);
endmodule
