// Logisim project Flash.circ as structural Verilog: 1 circuit, main circuit SST39SF010
module SST39SF010 (
  input  [16:0] A,
  input  CSn,
  input  OEn,
  output [7:0] D
);

  wire nor_1_out;
  wire [7:0] rom_1_data;

  ROM #(.addrWidth(17)) rom_1 (.addr(A), .data(rom_1_data));
  nor nor_1 (nor_1_out, CSn, OEn);
  assign D[0] = nor_1_out ? rom_1_data[0] : 1'bz;  // Controlled_Buffer controlled_buffer_1
  assign D[1] = nor_1_out ? rom_1_data[1] : 1'bz;  // Controlled_Buffer controlled_buffer_2
  assign D[2] = nor_1_out ? rom_1_data[2] : 1'bz;  // Controlled_Buffer controlled_buffer_3
  assign D[3] = nor_1_out ? rom_1_data[3] : 1'bz;  // Controlled_Buffer controlled_buffer_4
  assign D[4] = nor_1_out ? rom_1_data[4] : 1'bz;  // Controlled_Buffer controlled_buffer_5
  assign D[5] = nor_1_out ? rom_1_data[5] : 1'bz;  // Controlled_Buffer controlled_buffer_6
  assign D[6] = nor_1_out ? rom_1_data[6] : 1'bz;  // Controlled_Buffer controlled_buffer_7
  assign D[7] = nor_1_out ? rom_1_data[7] : 1'bz;  // Controlled_Buffer controlled_buffer_8
endmodule
